# Fritzing sketch parking sensor (saved by Fritzing 0.9.3b)

parts:
  Parça1 = Arduino Uno (Rev3)
  hc-sr1 = hc-sr04

nets:
  N1: Parça1.D6_PWM, hc-sr1.Echo
  N2: Parça1.D7, hc-sr1.Trig
  5V: Parça1.5V, hc-sr1.VCC
  GND: Parça1.GND, hc-sr1.GND
